# Fritzing sketch F Stop Timer (saved by Fritzing 1.0.2b)
circuit board: 11cm x 8.2cm
breadboards: 1

parts:
  U1 = LuaNode32 / ESP32 [part_number=ESP32S-PIN30]
  Display_Data = Screw terminal - 2 pins [package=THT]
  GND/5v = Screw terminal - 2 pins [package=THT]
  Mode/Focus = Screw terminal - 2 pins [package=THT]
  Light/Start = Screw terminal - 2 pins [package=THT]
  Encoder = Screw terminal - 2 pins [package=THT]
  D1 = Screw terminal - 2 pins [package=THT]
  D2 = Screw terminal - 2 pins [package=THT]
  Print_1 = Screw terminal - 2 pins [package=THT]
  Print_2 = Screw terminal - 2 pins [package=THT]
  Print_3 = Screw terminal - 2 pins [package=THT]
  Print_4 = Screw terminal - 2 pins [package=THT]
  Step_1 = Screw terminal - 2 pins [package=THT]
  Step_2 = Screw terminal - 2 pins [package=THT]
  Step_3 = Screw terminal - 2 pins [package=THT]
  Step_4 = Screw terminal - 2 pins [package=THT]
  IC2 = MCP23017 I2C I/O Expander
  LED1 = LED - 5mm [color="Red (633nm)" current=0.030A package="5 mm [THT]"]
  LED2 = LED - 5mm [color="Red (633nm)" current=0.030A package="5 mm [THT]"]
  LED3 = LED - 5mm [color="Red (633nm)" current=0.030A package="5 mm [THT]"]
  LED4 = LED - 5mm [color="Red (633nm)" current=0.030A package="5 mm [THT]"]
  GND/3v = Screw terminal - 2 pins [package=THT]
  R1 = Resistor [tolerance=±5% power=0.25W resistance=100 package=THT]

nets:
  N1: U1.D32, Encoder.pin2
  N2: U1.D33, Encoder.pin1
  N3: U1.D25, D1.pin2
  N4: U1.D26, D1.pin1
  N5: U1.D27, D2.pin2
  N6: U1.D14, D2.pin1
  N7: U1.D12, Mode/Focus.pin2
  N8: U1.D13, Light/Start.pin1
  GND: U1.GND, GND/5v.pin2, IC2.VSS, IC2.A0, IC2.A1, IC2.A2, LED1.anode, LED2.anode, LED3.anode, LED4.anode, GND/3v.pin2
  N9: U1.Vin, GND/5v.pin1, R1.Pin_1
  3V3: U1.3V3, IC2.VDD, IC2.RESET, GND/3v.pin1
  N10: U1.D15, Light/Start.pin2
  N11: U1.D5, Mode/Focus.pin1
  N12: U1.D21, Display_Data.pin2, IC2.SDA
  N13: U1.D22, Display_Data.pin1, IC2.SCL
  N14: Print_1.pin1, IC2.GPA1
  N15: Print_1.pin2, IC2.GPA0
  N16: Print_2.pin1, IC2.GPA3
  N17: Print_2.pin2, IC2.GPA2
  N18: Print_3.pin1, IC2.GPA5
  N19: Print_3.pin2, IC2.GPA4
  N20: Print_4.pin2, IC2.GPA6
  N21: Step_1.pin1, IC2.GPB1
  N22: Step_1.pin2, IC2.GPB0
  N23: Step_2.pin1, IC2.GPB3
  N24: Step_2.pin2, IC2.GPB2
  N25: Step_3.pin1, IC2.GPB5
  N26: Step_3.pin2, IC2.GPB4
  N27: Step_4.pin2, IC2.GPB6
  N28: LED1.cathode, LED2.cathode, LED3.cathode, LED4.cathode, R1.Pin_0

notes:
  F Stop Timer Controller by John Jones

custom parts:
  LuaNode32 / ESP32: New Image for LuaNode32 DOIT ESP32 DEVKIT V1. Base parts from LuaNode32 / ESP32 ESP32 based LuaNode32 by G.Noorlander DOIT Esp32 DevKit v1 (30 pins long, 11 pins width) by Werner Rothschopf (modified by vanepp Dec 2018)
  MCP23017 I2C I/O Expander: The MCP23017 uses two i2c pins (these can be shared with other i2c devices), and in exchange gives you 16 general purpose pins. You can set each of 16 pins to be input, output, input with a pullup or open drain. There's even the ability to get an interrupt via an external pin when any of the inputs change so you don't have to keep polling the chip.
